# Fritzing sketch station-electric-scheme (saved by Fritzing 0.9.10b)
breadboards: 1

parts:
  Bottom_Lifthill = Hall Sensor [part_number=A3144 package=TO92]
  Exit_Station = Hall Sensor [part_number=A3144 package=TO92]
  Start_Position = Hall Sensor [part_number=A3144 package=TO92]
  Enter_Station = Hall Sensor [part_number=A3144 package=TO92]
  Stationstepper_+_driver = 28BYJ-48 Stepper Motor [part_number=28BYJ-48]  # not connected
  Stepper_Driver = 28BYJ-48 Driver Module [part_number=ULN2003 package=THT]
  Lifthill_Steppermotor = 28BYJ-48 Stepper Motor [part_number=28BYJ-48]  # not connected
  Station_ESP = ESP32 DevKitc V4
  Lifthillstepper_+_driver = 28BYJ-48 Driver Module [part_number=ULN2003 package=THT]
  12V_DC = Power plug
  12DC_->_5DC = Voltage Regulator - 5V [package="TO220 [THT]"]
  R1 = Resistor [tolerance=±5% power=0.25 resistance=10k package=THT]
  part = Resistor [tolerance=±5% power=0.5W resistance=10k part_number=R2 package=THT]
  R3 = Resistor [tolerance=±5% power=0.25 resistance=10k package=THT]
  R4 = Resistor [tolerance=±5% power=0.25 resistance=10k package=THT]

nets:
  GND: Bottom_Lifthill.GND, Exit_Station.GND, Start_Position.GND, Enter_Station.GND, Lifthillstepper_+_driver.Vmotor, 12DC_->_5DC.output_voltage, R1.Pin_0, part.Pin_0, R3.Pin_0, R4.Pin_0
  N1: Bottom_Lifthill.OUT, Station_ESP.IO32, R1.Pin_1
  N2: Exit_Station.OUT, Station_ESP.IO33, part.Pin_1
  N3: Start_Position.OUT, Station_ESP.IO25, R3.Pin_1
  N4: Enter_Station.OUT, Station_ESP.IO26, R4.Pin_1
  N5: Stepper_Driver.IN1, Station_ESP.IO18
  N6: Stepper_Driver.IN2, Station_ESP.IO19
  N7: Stepper_Driver.IN3, Station_ESP.IO22
  N8: Stepper_Driver.IN4, Station_ESP.IO23
  GND_2: Stepper_Driver.GND, Station_ESP.GND, Lifthillstepper_+_driver.GND, 12V_DC.GND, 12DC_->_5DC.GND
  N9: Stepper_Driver.Vmotor, Station_ESP.3V3
  N10: Station_ESP.IO27, Lifthillstepper_+_driver.IN4
  N11: Station_ESP.IO14, Lifthillstepper_+_driver.IN3
  N12: Station_ESP.IO12, Lifthillstepper_+_driver.IN2
  N13: Station_ESP.IO13, Lifthillstepper_+_driver.IN1
  N14: 12V_DC.VCC, 12DC_->_5DC.input_voltage

custom parts:
  Hall Sensor: A Hall Sensor
  28BYJ-48 Stepper Motor: Unipolar Stepper Motor 28BYJ-48 Top coil - pink & orange Bottom coil - blue & yellow Common rail - red Connector pins: blue - pink - yellow - orange - red
  28BYJ-48 Driver Module: High-power ULN2003 Stepper Motor Driver Board Test Module For Arduino AVR SMD
  ESP32 DevKitc V4: ESP32-DevKitC board with ESP32-WROOM-32 module. ESP32-DevKitC V4 is a small-sized ESP32-based development board produced by Espressif. Most of the pins on the ESP module are broken out to the pin headers on the board. The pins D0, D1, D2, D3, CMD and CLK are used internally for communication between ESP32 and SPI flash memory. They are grouped on both sides near the USB connector. Avoid using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
